# Fritzing sketch phase_1_design (saved by Fritzing 0.7.10b)
breadboards: 1

parts:
  Arduino1 = Arduino
  M1 = DC Motor
  IC1 = L293D [package=THT]
  S1 = Toggle Switch [package=THT]

nets:
  N1: Arduino1.GND, IC1.0V, S1.COM
  N2: Arduino1.D10, IC1.In_1
  N3: Arduino1.D9, IC1.In_2
  N4: Arduino1.D8, S1.L2
  N5: Arduino1.+5V, IC1.+V
  N6: M1.pin_1, IC1.Out_1_(_Controlled_by_Enable_1_)
  N7: M1.pin_2, IC1.Out_2_(_Controlled_by_Enable_1_)
  N8: IC1.Enable_1, IC1.Enable_2, S1.L1
